# Fritzing sketch SimpleI2sSpeaker (saved by Fritzing 0.9.10b)

parts:
  Mod1 = Raspberry Pi Pico
  パーツ1 = Adafruit MAX98357A I2S 3W Class D Amplifier [part_number="Adafruit #3006"]
  J1 = Piezo Speaker

nets:
  N1: Mod1.pin_3, Mod1.pin_23, パーツ1.GND
  N2: Mod1.pin_17, パーツ1.BCLK
  N3: Mod1.pin_19, パーツ1.LRCLK
  N4: Mod1.pin_20, パーツ1.DIN
  N5: Mod1.pin_36, パーツ1.VIN
  N6: パーツ1.VO-, J1.pin1
  N7: パーツ1.VO+, J1.pin2

custom parts:
  Raspberry Pi Pico: Raspberry Pi Pico. Based around the RP2040 microcontroller the Pico is a low cost microcontroller device bringing Raspberry Pi quality, cost, and easy of use to the microcontroller space. Jan 2021, Split part in to two versions: tht (this one) and SMD. This one will drill holes for a .1 in header in pcb to allow plugging in the module as well as providing pads to solder the module to the top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
  Adafruit MAX98357A I2S 3W Class D Amplifier: Listen to this good news - we now have an all in one digital audio amp breakout board that works incredibly well with the Raspberry Pi! If you're looking for an easy and low cost way to get you digital sound files bumpin' then the MAX08357 I2S Amp Breakout is for you. It takes standard I2S digital audio input and, not only decodes it into analog, but also amplifies it directly into a speaker.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
